// Logisim project ETFStudent.circ as structural Verilog: 10 circuits, main circuit REG32_LD
module REG32_LD (
  input  [31:0] I15__0,
  input  LD,
  input  mr,
  input  CLK,
  output [31:0] A15__0
);

  // REG16_LD reg16_ld_1: pin names not known; wires that end beside it: CLK, mr, I15__0[31:16], A15__0[31:16], LD
  // REG16_LD reg16_ld_2: pin names not known; wires that end beside it: CLK, mr, I15__0[15:0], A15__0[15:0], LD

  // Notes on the sheet:
  //   __
endmodule

module KMADR (
  input  pcrel,
  input  immed,
  input  memdir,
  input  regdir,
  input  regind,
  output [3:0] Adr3__0
);

  assign Adr3__0 = immed ? 4'b0010 : 4'bz;  // Controlled_Buffer controlled_buffer_1
  assign Adr3__0 = memdir ? 4'b0011 : 4'bz;  // Controlled_Buffer controlled_buffer_2
  assign Adr3__0 = regdir ? 4'b1000 : 4'bz;  // Controlled_Buffer controlled_buffer_3
  assign Adr3__0 = regind ? 4'b1010 : 4'bz;  // Controlled_Buffer controlled_buffer_4
  assign Adr3__0 = pcrel ? 4'b1111 : 4'bz;  // Controlled_Buffer controlled_buffer_5
endmodule

module KMOPR (
  input  LD,
  input  ST,
  input  ADD,
  input  SUB,
  input  BLSS,
  input  JLEQ,
  input  JMP,
  input  JSR,
  input  RTS,
  input  RTI,
  input  HALT,
  output [5:0] Adr5__0
);

  assign Adr5__0 = LD ? 6'b000010 : 6'bz;  // Controlled_Buffer controlled_buffer_1
  assign Adr5__0 = ST ? 6'b000100 : 6'bz;  // Controlled_Buffer controlled_buffer_2
  assign Adr5__0 = ADD ? 6'b001010 : 6'bz;  // Controlled_Buffer controlled_buffer_3
  assign Adr5__0 = SUB ? 6'b001100 : 6'bz;  // Controlled_Buffer controlled_buffer_4
  assign Adr5__0 = BLSS ? 6'b001110 : 6'bz;  // Controlled_Buffer controlled_buffer_5
  assign Adr5__0 = JLEQ ? 6'b010000 : 6'bz;  // Controlled_Buffer controlled_buffer_6
  assign Adr5__0 = JMP ? 6'b010001 : 6'bz;  // Controlled_Buffer controlled_buffer_7
  assign Adr5__0 = JSR ? 6'b010010 : 6'bz;  // Controlled_Buffer controlled_buffer_8
  assign Adr5__0 = RTS ? 6'b010111 : 6'bz;  // Controlled_Buffer controlled_buffer_9
  assign Adr5__0 = RTI ? 6'b011110 : 6'bz;  // Controlled_Buffer controlled_buffer_10
  assign Adr5__0 = HALT ? 6'b100010 : 6'bz;  // Controlled_Buffer controlled_buffer_11
endmodule

module REG6_INC_LD (
  input  [5:0] I5__0,
  input  LD,
  input  INC,
  input  mr,
  input  CLK,
  output [5:0] A5__0
);

  wire reg2m_inc_ld_1_p7, reg2m_inc_ld_2_p8;

  // REG2m_INC_LD reg2m_inc_ld_1: pin names not known; wires that end beside it: CLK, mr, I5__0[5:4], A5__0[5:4], LD, INC, reg2m_inc_ld_1_p7
  // REG2m_INC_LD reg2m_inc_ld_2: pin names not known; wires that end beside it: CLK, reg2m_inc_ld_1_p7, mr, I5__0[3:2], A5__0[3:2], LD, INC, reg2m_inc_ld_2_p8
  // REG2m_INC_LD reg2m_inc_ld_3: pin names not known; wires that end beside it: CLK, reg2m_inc_ld_2_p8, mr, I5__0[1:0], A5__0[1:0], LD, INC, INC

  // Notes on the sheet:
  //   __
endmodule

module ROM32x24 (
  input  [4:0] A4__0,
  input  CS,
  output [23:0] DOUT
);

  ROM #(.addrWidth(5), .dataWidth(24)) rom_1 (.addr(A4__0), .data(DOUT), .sel(CS));
endmodule

module ROM32X20 (
  input  [4:0] A4__0,
  input  CS,
  output [19:0] DOUT
);

  ROM #(.addrWidth(5), .dataWidth(20)) rom_1 (.addr(A4__0), .data(DOUT), .sel(CS));
endmodule

module ALU_ADD_AND_OR (
  input  Cin,
  input  [15:0] A,
  input  [15:0] B,
  input  add,
  input  \or ,
  input  \and ,
  input  asl,
  output [15:0] F,
  output Cout
);

  wire adder_1_cout;
  wire [15:0] adder_1_out, and_1_out, or_1_out, shifter_1_out;

  Adder #(.width(16)) adder_1 (.a(A), .b(B), .out(adder_1_out), .cin(Cin), .cout(adder_1_cout));
  assign F = add ? adder_1_out : 16'bz;  // Controlled_Buffer controlled_buffer_1
  assign Cout = add ? adder_1_cout : 1'bz;  // Controlled_Buffer controlled_buffer_2
  assign or_1_out = A | B;  // OR_Gate or_1, 16 bits wide
  assign and_1_out = A & B;  // AND_Gate and_1, 16 bits wide
  Shifter #(.width(16)) shifter_1 (.in(A), .\dist (4'b0001), .out(shifter_1_out));
  assign F = \or  ? or_1_out : 16'bz;  // Controlled_Buffer controlled_buffer_3
  assign F = \and  ? and_1_out : 16'bz;  // Controlled_Buffer controlled_buffer_4
  assign F = asl ? shifter_1_out : 16'bz;  // Controlled_Buffer controlled_buffer_5
endmodule

module ROM128x51 (
  input  [6:0] A6__0,
  input  CS,
  output [31:0] DOUT31__0,
  output [6:0] DOUT50__44,
  output [11:0] DOUT43__32
);

  ROM #(.addrWidth(7), .dataWidth(7)) rom_1 (.addr(A6__0), .data(DOUT50__44), .sel(CS));
  ROM #(.addrWidth(7), .dataWidth(12)) rom_2 (.addr(A6__0), .data(DOUT43__32), .sel(CS));
  ROM #(.addrWidth(7), .dataWidth(32)) rom_3 (.addr(A6__0), .data(DOUT31__0), .sel(CS));
endmodule

module KMOPR1 (
  input  LD,
  input  ST,
  input  ADD,
  input  AND,
  input  OR,
  input  JADR,
  input  JMP,
  input  BR,
  input  BEQL,
  input  BNEG,
  input  BGRT,
  input  BGREU,
  input  JLEQ,
  input  HALT,
  input  ASL,
  input  STIVTP,
  input  PUSH,
  input  POP,
  input  JSR,
  input  RTS,
  input  RTI,
  input  ABS,
  input  SWAP,
  output [6:0] Adr6__0
);

  assign Adr6__0 = LD ? 7'b0000010 : 7'bz;  // Controlled_Buffer controlled_buffer_1
  assign Adr6__0 = ST ? 7'b0000100 : 7'bz;  // Controlled_Buffer controlled_buffer_2
  assign Adr6__0 = ADD ? 7'b0001011 : 7'bz;  // Controlled_Buffer controlled_buffer_3
  assign Adr6__0 = AND ? 7'b0001101 : 7'bz;  // Controlled_Buffer controlled_buffer_4
  assign Adr6__0 = OR ? 7'b0001111 : 7'bz;  // Controlled_Buffer controlled_buffer_5
  assign Adr6__0 = JADR ? 7'b0010100 : 7'bz;  // Controlled_Buffer controlled_buffer_6
  assign Adr6__0 = JMP ? 7'b0010101 : 7'bz;  // Controlled_Buffer controlled_buffer_7
  assign Adr6__0 = BR ? 7'b0010110 : 7'bz;  // Controlled_Buffer controlled_buffer_8
  assign Adr6__0 = BEQL ? 7'b0010111 : 7'bz;  // Controlled_Buffer controlled_buffer_9
  assign Adr6__0 = BNEG ? 7'b0010111 : 7'bz;  // Controlled_Buffer controlled_buffer_10
  assign Adr6__0 = BGRT ? 7'b0010111 : 7'bz;  // Controlled_Buffer controlled_buffer_11
  assign Adr6__0 = BGREU ? 7'b0010111 : 7'bz;  // Controlled_Buffer controlled_buffer_12
  assign Adr6__0 = JLEQ ? 7'b0011001 : 7'bz;  // Controlled_Buffer controlled_buffer_13
  assign Adr6__0 = HALT ? 7'b0011011 : 7'bz;  // Controlled_Buffer controlled_buffer_14
  assign Adr6__0 = ASL ? 7'b0010001 : 7'bz;  // Controlled_Buffer controlled_buffer_15
  assign Adr6__0 = STIVTP ? 7'b0011100 : 7'bz;  // Controlled_Buffer controlled_buffer_16
  assign Adr6__0 = PUSH ? 7'b0011101 : 7'bz;  // Controlled_Buffer controlled_buffer_17
  assign Adr6__0 = POP ? 7'b0100011 : 7'bz;  // Controlled_Buffer controlled_buffer_18
  assign Adr6__0 = JSR ? 7'b0101011 : 7'bz;  // Controlled_Buffer controlled_buffer_19
  assign Adr6__0 = RTS ? 7'b0110001 : 7'bz;  // Controlled_Buffer controlled_buffer_20
  assign Adr6__0 = RTI ? 7'b1001010 : 7'bz;  // Controlled_Buffer controlled_buffer_21
  assign Adr6__0 = ABS ? 7'b0111101 : 7'bz;  // Controlled_Buffer controlled_buffer_22
  assign Adr6__0 = SWAP ? 7'b0111111 : 7'bz;  // Controlled_Buffer controlled_buffer_23
endmodule

module ROM64x31 (
  input  [5:0] A5__0,
  input  CS,
  output [30:0] DOUT
);

  ROM #(.addrWidth(6), .dataWidth(31)) rom_1 (.addr(A5__0), .data(DOUT), .sel(CS));
endmodule
