// Logisim project ORT2Project.circ as structural Verilog: 8 circuits, main circuit COMPUTER
module COMPUTER (
);

  wire BTN_INTR0_out, BTN_INTR1_out, BTN_INTR2_out, BTN_INTR3_out, BTN_RST_out, CLK, cpu_1_inta,
       pull_resistor_2_node, pull_resistor_5_node, ram_1_out_8, rst;
  wire [1:0] cpu_1_uext1__0;
  wire [3:0] interrupt_interface_4_1_intr3__0;
  wire [7:0] pull_resistor_1_node, ram_1_out_7;
  wire [15:0] pull_resistor_4_node;

  Button BTN_RST (.out(BTN_RST_out));
  Clock u_CLK (.out(CLK));
  // RisingEdge risingedge_1: pin names not known; wires that end beside it: BTN_RST_out, CLK, rst
  RAM ram_1 (
    .in_1(pull_resistor_4_node), .in_2(CLK), .in_3(pull_resistor_1_node), .in_4(pull_resistor_2_node),
    .in_5(pull_resistor_5_node), .in_6(rst), .out_7(ram_1_out_7), .out_8(ram_1_out_8));
  Pull_Resistor pull_resistor_1 (.node(pull_resistor_1_node));
  Pull_Resistor pull_resistor_2 (.node(pull_resistor_2_node));
  Pull_Resistor pull_resistor_3 (.node(ram_1_out_7));
  Pull_Resistor pull_resistor_4 (.node(pull_resistor_4_node));
  Pull_Resistor pull_resistor_5 (.node(pull_resistor_5_node));
  Pull_Resistor pull_resistor_6 (.node(ram_1_out_8));
  CPU cpu_1 (
    .in_1(rst), .in_2(CLK), .in_3(ram_1_out_8), .in_4(ram_1_out_7), .ABUS(pull_resistor_4_node),
    .DOUTBUS(pull_resistor_1_node), .out_8(pull_resistor_2_node), .out_9(pull_resistor_5_node),
    .inta(cpu_1_inta), .intr3__0(interrupt_interface_4_1_intr3__0), .UEXT1__0(cpu_1_uext1__0));
  INTERRUPT_INTERFACE_4 interrupt_interface_4_1 (
    .BTN_INTR0(BTN_INTR0_out), .BTN_INTR1(BTN_INTR1_out), .BTN_INTR2(BTN_INTR2_out),
    .BTN_INTR3(BTN_INTR3_out), .inta(cpu_1_inta), .UEXT1__0(cpu_1_uext1__0), .CLK(CLK),
    .intr3__0(interrupt_interface_4_1_intr3__0));
  Button BTN_INTR3 (.out(BTN_INTR3_out));
  Button BTN_INTR2 (.out(BTN_INTR2_out));
  Button BTN_INTR1 (.out(BTN_INTR1_out));
  Button BTN_INTR0 (.out(BTN_INTR0_out));
endmodule

module CPU (
  input  in_1,
  input  in_2,
  input  in_3,
  input  [7:0] in_4,
  input  [3:0] intr3__0,
  output [15:0] ABUS,
  output [7:0] DOUTBUS,
  output out_8,
  output out_9,
  output inta,
  output [1:0] UEXT1__0
);

  wire [3:0] common_1_phaseffbus;
  wire [4:0] common_1_addrbus;
  wire [7:0] DWH, DWL, PSW, pull_resistor_3_node, pull_resistor_5_node;
  wire [14:0] pull_resistor_4_node;
  wire [15:0] A, B, INTRADDR, IVTP;
  wire [16:0] ALU, pull_resistor_7_node;
  wire [24:0] common_1_instrucbus;

  COMMON common_1 (
    .CLK(in_2), .RST(in_1), .DIN(in_4), .CMEMBUS(pull_resistor_4_node), .MAR(ABUS), .MDR(DOUTBUS),
    .PHASEFFBUS(common_1_phaseffbus), .INSTRUCBUS(common_1_instrucbus), .ADDRBUS(common_1_addrbus),
    .PSW(PSW), .CREGBUS(pull_resistor_7_node), .CFFBUS(pull_resistor_5_node), .B(B), .A(A),
    .CPSW(pull_resistor_3_node), .ALU(ALU), .IVTPPDSP(INTRADDR), .DWH(DWH), .DWL(DWL), .IVTP(IVTP));
  Pull_Resistor pull_resistor_1 (.node(common_1_instrucbus));
  Pull_Resistor pull_resistor_2 (.node(common_1_phaseffbus));
  Pull_Resistor pull_resistor_3 (.node(pull_resistor_3_node));
  Pull_Resistor pull_resistor_4 (.node(pull_resistor_4_node));
  Pull_Resistor pull_resistor_5 (.node(pull_resistor_5_node));
  Pull_Resistor pull_resistor_6 (.node(common_1_addrbus));
  Pull_Resistor pull_resistor_7 (.node(pull_resistor_7_node));
  FETCH fetch_1 (
    .in_1(in_1), .in_2(in_2), .in_3(in_3), .PHASEFFBUS(common_1_phaseffbus),
    .INSTRUCBUS(common_1_instrucbus), .ADDRBUS(common_1_addrbus), .PSW(PSW), .rdMEM(out_9),
    .CMEMBUS(pull_resistor_4_node), .CFFBUS(pull_resistor_5_node), .CREGBUS(pull_resistor_7_node));
  ADDR addr_1 (
    .in_1(in_1), .in_2(in_2), .in_3(in_3), .PHASEFFBUS(common_1_phaseffbus), .ADDRBUS(common_1_addrbus),
    .rdMEM(out_9), .CMEMBUS(pull_resistor_4_node), .CFFBUS(pull_resistor_5_node),
    .CREGBUS(pull_resistor_7_node), .INSTRUCBUS(common_1_instrucbus));
  EXEC exec_1 (
    .in_1(in_1), .in_2(in_2), .in_3(in_3), .B(B), .PHASEFFBUS(common_1_phaseffbus),
    .INSTRUCBUS(common_1_instrucbus), .ADDRBUS(common_1_addrbus), .PSW(PSW), .A(A), .ALU(ALU),
    .CMEMBUS(pull_resistor_4_node), .CFFBUS(pull_resistor_5_node), .CREGBUS(pull_resistor_7_node),
    .CPSW(pull_resistor_3_node), .rdMEM(out_9), .wrMEM(out_8), .DWH(DWH), .DWL(DWL));
  INTR intr_1 (
    .in_2(in_1), .in_3(in_2), .in_4(in_3), .PHASEFFBUS(common_1_phaseffbus),
    .INSTRUCBUS(common_1_instrucbus), .PSW(PSW), .intr(intr3__0), .ADDIVTP(INTRADDR),
    .CMEMBUS(pull_resistor_4_node), .CFFBUS(pull_resistor_5_node), .CREGBUS(pull_resistor_7_node),
    .rdMEM(out_9), .wrMEM(out_8), .UEXT1__0(UEXT1__0), .inta(inta), .IVTP(IVTP));

  // Other names for the same wires on the sheet: CLK = in_2; DIN7__0[7:0] = in_4; FCBUS = in_3; MAR[15:0] = ABUS;
  //   MDR[7:0] = DOUTBUS; RD = out_9; rst = in_1; WR = out_8
endmodule

module COMMON (
  input  CLK,
  input  RST,
  input  [7:0] DIN,
  input  [15:0] A,
  input  [16:0] ALU,
  input  [15:0] IVTPPDSP,
  input  [14:0] CMEMBUS,
  input  [7:0] CFFBUS,
  input  [16:0] CREGBUS,
  input  [7:0] CPSW,
  output [15:0] MAR,
  output [7:0] MDR,
  output [3:0] PHASEFFBUS,
  output [24:0] INSTRUCBUS,
  output [4:0] ADDRBUS,
  output [7:0] PSW,
  output [15:0] B,
  output [7:0] DWH,
  output [7:0] DWL,
  output [15:0] IVTP
);

  wire ADRINST, adrinst_t, and_1_out, and_2_out, and_3_out, and_4_out, and_5_out, and_6_out, and_7_out,
       and_8_out, and_9_out, and_10_out, and_11_out, and_12_out, and_13_out, and_14_out, and_15_out,
       and_16_out, and_17_out, and_18_out, and_19_out, and_20_out, and_21_out, and_22_out, and_23_out,
       and_24_out, bezadrinst, brunchinst, jmpinst, mp2_16b_1_p3, mp2_16b_2_p3, mp4_16b_1_p5, mp4_16b_2_p5,
       mp8_8b_1_p8, mp8_8b_1_p12, mp8_16b_1_p8, not_1_out, not_4_out, not_5_out, or_2_out, or_3_out,
       or_4_out, or_5_out, or_6_out, or_7_out, or_8_out, or_9_out, or_10_out, or_11_out, reg16_inc_ld_2_p4,
       rsff_2_p4, rsff_3_p4, rsff_5_p4, rsff_6_p4, rsff_8_p4, rsff_9_p4, rsff_10_p3, rsff_10_p4;
  wire [3:0] IR19__16, IR27__24, mp8_4b_1_p10;
  wire [7:0] IR7__0, IR15__8, reg8_ld_2_p3;
  wire [7:4] IR23__16, IR31__24;
  wire [15:0] ADDPCREL15__0, ADDW15__0, GPR15__0, mp2_16b_3_p3, PC15__0, SP15__0;

  // REG8_LD reg8_ld_1: pin names not known; wires that end beside it: CLK, MDR, {IR31__24, IR27__24}, CREGBUS[7]
  // MP8_16b mp8_16b_1: pin names not known; wires that end beside it: CMEMBUS[7], CMEMBUS[8], CMEMBUS[5], PC15__0, {IR15__8, IR7__0}, ADDW15__0, GPR15__0, mp8_16b_1_p8, SP15__0, IVTPPDSP, 1'b1
  // REG16_INC_LD reg16_inc_ld_1: pin names not known; wires that end beside it: CLK, mp8_16b_1_p8, MAR, CMEMBUS[0], CMEMBUS[1]
  // REG8_LD reg8_ld_2: pin names not known; wires that end beside it: CLK, MDR, reg8_ld_2_p3, CREGBUS[3]
  // REG8_LD reg8_ld_3: pin names not known; wires that end beside it: CLK, MDR, {IR23__16, IR19__16}, CREGBUS[6]
  // DC4_16 dc4_16_1: pin names not known; wires that end beside it: IR27__24, brunchinst, INSTRUCBUS[11], INSTRUCBUS[12], INSTRUCBUS[13], INSTRUCBUS[14], INSTRUCBUS[15]
  // REG8_LD reg8_ld_4: pin names not known; wires that end beside it: CLK, MDR, DWH, CREGBUS[10]
  // DC4_16 dc4_16_2: pin names not known; wires that end beside it: IR31__24, PSW[0], bezadrinst, brunchinst, jmpinst, adrinst_t
  // MP4_16b mp4_16b_1: pin names not known; wires that end beside it: CREGBUS[0], CREGBUS[1], {reg8_ld_2_p3, MDR}, {IR15__8, IR7__0}, mp4_16b_1_p5, GPR15__0, 1'b1
  // REG16_LD reg16_ld_1: pin names not known; wires that end beside it: CLK, mp4_16b_1_p5, B, CREGBUS[2]
  // REG8_LD reg8_ld_5: pin names not known; wires that end beside it: CLK, MDR, DWL, CREGBUS[11]
  // REG8_LD reg8_ld_6: pin names not known; wires that end beside it: CLK, MDR, IR15__8, CREGBUS[5]
  // MP8_8b mp8_8b_1: pin names not known; wires that end beside it: CMEMBUS[9], CMEMBUS[10], CMEMBUS[6], DIN, A[15:8], A[7:0], PC15__0[15:8], mp8_8b_1_p8, PC15__0[7:0], {PSW[5], {7{1'b0}}}, {3'b000, PSW[2], PSW[3], PSW[1], PSW[4], PSW[0]}, mp8_8b_1_p12, 1'b1
  // REG8_LD reg8_ld_7: pin names not known; wires that end beside it: CLK, mp8_8b_1_p8, MDR, CMEMBUS[2]
  // DC4_16 dc4_16_3: pin names not known; wires that end beside it: IR27__24, jmpinst, INSTRUCBUS[8], INSTRUCBUS[9], INSTRUCBUS[10]
  // DC4_16 dc4_16_4: pin names not known; wires that end beside it: IR27__24, bezadrinst, INSTRUCBUS[0], INSTRUCBUS[1], INSTRUCBUS[2], INSTRUCBUS[3], INSTRUCBUS[4], INSTRUCBUS[5], INSTRUCBUS[6], INSTRUCBUS[7]
  // MP2_8b mp2_8b_1: pin names not known; wires that end beside it: CREGBUS[15], GPR15__0[15:8], mp8_8b_1_p12, GPR15__0[7:0], 1'b1
  // REG8_LD reg8_ld_8: pin names not known; wires that end beside it: CLK, MDR, IR7__0, CREGBUS[4]
  // DC4_16 dc4_16_5: pin names not known; wires that end beside it: IR23__16, adrinst_t, ADDRBUS[0], ADDRBUS[1], ADDRBUS[2], ADDRBUS[3], ADDRBUS[4]
  // MP4_16b mp4_16b_2: pin names not known; wires that end beside it: CMEMBUS[11], CMEMBUS[12], {IR23__16, IR19__16, IR15__8}, ADDPCREL15__0, mp4_16b_2_p5, {DWH, DWL}, MAR, 1'b1
  // DC4_16 dc4_16_6: pin names not known; wires that end beside it: IR27__24, adrinst_t, INSTRUCBUS[16], INSTRUCBUS[17], INSTRUCBUS[18], INSTRUCBUS[22], INSTRUCBUS[19], INSTRUCBUS[21], INSTRUCBUS[20]
  // ADD16 add16_1: pin names not known; wires that end beside it: {{13{IR19__16[3]}}, IR19__16[2:0]}, ADDW15__0, PC15__0
  // ADD16 add16_2: pin names not known; wires that end beside it: {{9{IR23__16[7]}}, IR23__16[6:4], IR19__16}, ADDPCREL15__0, PC15__0
  not not_1 (not_1_out, RST);
  // RSFF rsff_1: pin names not known; wires that end beside it: CFFBUS[1], CLK, CFFBUS[0], not_1_out, PHASEFFBUS[0]
  // MP2_16b mp2_16b_1: pin names not known; wires that end beside it: RST, mp4_16b_2_p5, mp2_16b_1_p3, 16'h2000, 1'b1
  // REG16_INC_LD reg16_inc_ld_2: pin names not known; wires that end beside it: CLK, mp2_16b_1_p3, PC15__0, reg16_inc_ld_2_p4, CMEMBUS[4]
  or or_1 (reg16_inc_ld_2_p4, CMEMBUS[3], RST);
  // RSFF rsff_2: pin names not known; wires that end beside it: CFFBUS[3], CLK, CFFBUS[2], rsff_2_p4, PHASEFFBUS[1]
  not not_2 (rsff_2_p4, RST);
  or or_2 (or_2_out, INSTRUCBUS[6], INSTRUCBUS[2]);
  and and_1 (and_1_out, ~ALU[15], A[15], B[15]);  // AND_Gate
  and and_2 (and_2_out, ALU[15], ~A[15], ~B[15]);  // AND_Gate
  and and_3 (and_3_out, INSTRUCBUS[18], ALU[16]);
  and and_4 (and_4_out, INSTRUCBUS[3], A[15]);
  and and_5 (and_5_out, INSTRUCBUS[2], DWL[4]);
  // RSFF rsff_3: pin names not known; wires that end beside it: CFFBUS[5], CLK, CFFBUS[4], rsff_3_p4, PHASEFFBUS[2]
  not not_3 (rsff_3_p4, RST);
  or or_3 (or_3_out, ADRINST, INSTRUCBUS[3], INSTRUCBUS[7]);
  and and_6 (and_6_out, or_2_out, DWL[2]);
  or or_4 (or_4_out, and_1_out, and_2_out);
  or or_5 (or_5_out, and_3_out, and_4_out, and_5_out);
  not not_4 (not_4_out, RST);
  and and_7 (and_7_out, ~DWL[0], INSTRUCBUS[2], CPSW[6]);  // AND_Gate
  and and_8 (and_8_out, DWL[0], INSTRUCBUS[2], CPSW[6]);
  or or_6 (or_6_out, ADRINST, INSTRUCBUS[3]);
  and and_9 (and_9_out, or_6_out, and_10_out);
  and and_10 (and_10_out, ~A[0], ~A[1], ~A[2], ~A[3], ~A[4], ~A[5], ~A[6], ~A[7], ~A[8], ~A[9], ~A[10], ~A[11], ~A[12], ~A[13], ~A[14], ~A[15]);  // AND_Gate
  and and_11 (and_11_out, or_3_out, A[15]);
  and and_12 (and_12_out, INSTRUCBUS[18], or_4_out);
  and and_13 (and_13_out, INSTRUCBUS[2], DWL[3]);
  and and_14 (and_14_out, ~or_5_out, CPSW[2]);  // AND_Gate
  and and_15 (and_15_out, or_5_out, CPSW[2]);
  // REG16 reg16_1: pin names not known; wires that end beside it: CLK, 16'h8000, SP15__0, RST, CMEMBUS[13], CMEMBUS[14]
  // MP2_16b mp2_16b_2: pin names not known; wires that end beside it: RST, A, mp2_16b_2_p3, 16'hf000, 1'b1
  // REG16_LD reg16_ld_2: pin names not known; wires that end beside it: CLK, not_4_out, mp2_16b_2_p3, IVTP, CREGBUS[9]
  not not_5 (not_5_out, RST);
  or or_7 (or_7_out, and_7_out, CPSW[0]);
  // RSFF rsff_4: pin names not known; wires that end beside it: or_7_out, CLK, and_8_out, not_5_out, PSW[0]
  or or_8 (or_8_out, and_9_out, and_18_out);
  or or_9 (or_9_out, INSTRUCBUS[6], INSTRUCBUS[2]);
  or or_10 (or_10_out, and_11_out, and_6_out);
  or or_11 (or_11_out, and_12_out, and_13_out);
  // RSFF rsff_5: pin names not known; wires that end beside it: and_14_out, CLK, and_15_out, rsff_5_p4, PSW[3]
  not not_6 (rsff_5_p4, RST);
  // RSFF rsff_6: pin names not known; wires that end beside it: CFFBUS[7], CLK, CFFBUS[6], rsff_6_p4, PHASEFFBUS[3]
  not not_7 (rsff_6_p4, RST);
  or or_12 (ADRINST, INSTRUCBUS[16], INSTRUCBUS[18], INSTRUCBUS[22], INSTRUCBUS[19], INSTRUCBUS[20]);
  and and_16 (and_16_out, ~or_8_out, CPSW[4]);  // AND_Gate
  and and_17 (and_17_out, or_8_out, CPSW[4]);
  and and_18 (and_18_out, or_9_out, DWL[1]);
  and and_19 (and_19_out, ~or_10_out, CPSW[3]);  // AND_Gate
  and and_20 (and_20_out, CPSW[3], or_10_out);
  and and_21 (and_21_out, ~or_11_out, CPSW[2]);  // AND_Gate
  and and_22 (and_22_out, CPSW[2], or_11_out);
  // RSFF rsff_7: pin names not known; wires that end beside it: and_16_out, CLK, and_17_out, PSW[4]
  // NOT_Gate not_8 has open pins: in=RST, out=open
  // RSFF rsff_8: pin names not known; wires that end beside it: and_19_out, CLK, and_20_out, rsff_8_p4, PSW[1]
  not not_9 (rsff_8_p4, RST);
  // RSFF rsff_9: pin names not known; wires that end beside it: and_21_out, CLK, and_22_out, rsff_9_p4, PSW[2]
  not not_10 (rsff_9_p4, RST);
  and and_23 (and_23_out, DWH[7], INSTRUCBUS[2]);
  and and_24 (and_24_out, ~and_23_out, CPSW[1]);  // AND_Gate
  // RSFF rsff_10: pin names not known; wires that end beside it: and_24_out, CLK, rsff_10_p3, rsff_10_p4, PSW[5]
  not not_11 (rsff_10_p4, RST);
  and and_25 (rsff_10_p3, and_23_out, CPSW[1]);
  // MP8_4b mp8_4b_1: pin names not known; wires that end beside it: 4'b0011, 4'b0010, 4'b0001, 4'b0000, {1'b0, IR19__16[2:0]}, CREGBUS[12], 1'b1, CREGBUS[13], CREGBUS[14], mp8_4b_1_p10
  GPR8x16 gpr8x16_1 (.DI15__0(mp2_16b_3_p3), .A2__0(mp8_4b_1_p10[2:0]), .WR(CREGBUS[8]), .CLK(CLK), .DO15__0(GPR15__0));
  // MP2_16b mp2_16b_3: pin names not known; wires that end beside it: CREGBUS[16], A, mp2_16b_3_p3, {DWH, DWL}, 1'b1

  // Other names for the same wires on the sheet: MDR7__0[7:0] = MDR; IR23__16[3:0] = IR19__16; A15__0[15:0] = A;
  //   immed = ADDRBUS[0]; memdir = ADDRBUS[1]; regdir = ADDRBUS[2]; regind = ADDRBUS[3]; pcrel = ADDRBUS[4];
  //   ALU15__0[15:0] = ALU[15:0]; C16 = ALU[16]; B15__0[15:0] = B; stFETCH = CFFBUS[0]; clFETCH = CFFBUS[1];
  //   stADDR = CFFBUS[2]; clADDR = CFFBUS[3]; stEXEC = CFFBUS[4]; clEXEC = CFFBUS[5]; stINTR = CFFBUS[6];
  //   clINTR = CFFBUS[7]; ldMAR = CMEMBUS[0]; incMAR = CMEMBUS[1]; ldMDR = CMEMBUS[2]; ldPC = CMEMBUS[3];
  //   incPC = CMEMBUS[4]; mxMAR0 = CMEMBUS[5]; mxMDR0 = CMEMBUS[6]; mxMAR2 = CMEMBUS[7]; mxMAR1 = CMEMBUS[8];
  //   mxMDR2 = CMEMBUS[9]; mxMDR1 = CMEMBUS[10]; mxPC1 = CMEMBUS[11]; mxPC0 = CMEMBUS[12]; incSP = CMEMBUS[13];
  //   decSP = CMEMBUS[14]; clPSWSTART = CPSW[0]; ldI = CPSW[1]; ldV = CPSW[2]; ldN = CPSW[3]; ldZ = CPSW[4];
  //   ldC = CPSW[5]; ldSTART = CPSW[6]; mxB1 = CREGBUS[0]; mxB0 = CREGBUS[1]; ldB = CREGBUS[2]; ldP = CREGBUS[3];
  //   ldIR7__0 = CREGBUS[4]; ldIR15__8 = CREGBUS[5]; ldIR23__16 = CREGBUS[6]; ldIR31__24 = CREGBUS[7];
  //   wrGPR = CREGBUS[8]; ldIVTP = CREGBUS[9]; ldDWH = CREGBUS[10]; ldDWL = CREGBUS[11]; mxGPR2 = CREGBUS[12];
  //   mxGPR1 = CREGBUS[13]; mxGPR0 = CREGBUS[14]; mxGPR = CREGBUS[15]; reg = CREGBUS[16]; Din7__0[7:0] = DIN;
  //   ENTRADDR15__0[15:0] = IVTPPDSP; HALT = INSTRUCBUS[0]; RTS = INSTRUCBUS[1]; RTI = INSTRUCBUS[2];
  //   ASL = INSTRUCBUS[3]; STIVTP = INSTRUCBUS[4]; PUSH = INSTRUCBUS[5]; POP = INSTRUCBUS[6]; ABS = INSTRUCBUS[7];
  //   BR = INSTRUCBUS[8]; JMP = INSTRUCBUS[9]; JSR = INSTRUCBUS[10]; BEQL = INSTRUCBUS[11]; BNEG = INSTRUCBUS[12];
  //   BGRT = INSTRUCBUS[13]; BGREU = INSTRUCBUS[14]; JLEQ = INSTRUCBUS[15]; LD = INSTRUCBUS[16]; ST = INSTRUCBUS[17];
  //   ADD = INSTRUCBUS[18]; SWAP = INSTRUCBUS[19]; OR = INSTRUCBUS[20]; JADR = INSTRUCBUS[21]; AND = INSTRUCBUS[22];
  //   IR31__24[3:0] = IR27__24; IVTP15__0[15:0] = IVTP; MAR15__0[15:0] = MAR; FETCH = PHASEFFBUS[0];
  //   ADDR = PHASEFFBUS[1]; EXEC = PHASEFFBUS[2]; INTR = PHASEFFBUS[3]; PSW7__0[7:0] = PSW; PSWH[7] = PSW[5];
  //   PSWI = PSW[5]; PSWL[4:0] = {PSW[2], PSW[3], PSW[1], PSW[4], PSW[0]}; PSWSTART = PSW[0]; PSWZ = PSW[4];
  //   PSWN = PSW[1]; PSWC = PSW[3]; PSWV = PSW[2]

  // Notes on the sheet:
  //   Instrukcijski registar
  //   Pomocni registri
  //   MAR
  //   Dekoderi za prepoznavanje instrukcije na osnovu sadrzaja registra IR31..24
  //   MDR
  //   Sabirac za uslovne skokove
  //   Sabirac za pcrel
  //   FF za pokretanje FETCH, ADDR, EXEC i INTR faze izvršavanja instrukcije
  //   PC
  //   SP
  //   IVTP
  //   Programska statusna reč (PSW)
  //   Registarski fajl
endmodule

module FETCH (
  input  in_1,
  input  in_2,
  input  in_3,
  input  [3:0] PHASEFFBUS,
  input  [24:0] INSTRUCBUS,
  input  [4:0] ADDRBUS,
  input  [7:0] PSW,
  output [14:0] CMEMBUS,
  output [7:0] CFFBUS,
  output [16:0] CREGBUS,
  output rdMEM
);

  wire addr2, addr4, addr_t, and_1_out, and_2_out, and_3_out, and_4_out, and_5_out, and_8_out, and_9_out,
       and_10_out, and_11_out, and_12_out, and_13_out, and_14_out, and_15_out, bezadr1, bradr2, brbezadr1,
       brcnd, brgraddr, brgrinst, brjump2, brjump3, brnotfcmem, bruncnd, clFETCH, GRADDR, GRINST, incPC,
       jmp3, jump2, ldIR7__0, ldIR15__8, ldIR23__16, ldIR31__24, ldMAR, ldMDR, nor_1_out, not_1_out,
       not_3_out, not_4_out, not_5_out, notPSWSTandFETCH, or_4_out, or_5_out, or_9_out, or_10_out, or_11_out,
       or_13_out, rdMEM_t, reg8_inc_ld_1_p5, reg8_inc_ld_1_p6, stADDR, stEXEC;
  wire [3:0] rom32x24_1_dout_2;
  wire [7:0] reg8_inc_ld_1_p3, reg8_inc_ld_1_p4;
  wire [11:11] rom32x24_1_dout;

  or or_1 (bezadr1, INSTRUCBUS[0], INSTRUCBUS[1], INSTRUCBUS[2], INSTRUCBUS[3], INSTRUCBUS[4], INSTRUCBUS[5], INSTRUCBUS[6], INSTRUCBUS[7]);
  or or_2 (jump2, INSTRUCBUS[11], INSTRUCBUS[12], INSTRUCBUS[13], INSTRUCBUS[14], INSTRUCBUS[8]);
  not not_1 (not_1_out, in_1);
  // REG8_INC_LD reg8_inc_ld_1: pin names not known; wires that end beside it: in_2, not_1_out, reg8_inc_ld_1_p3, reg8_inc_ld_1_p4, reg8_inc_ld_1_p5, reg8_inc_ld_1_p6
  or or_3 (reg8_inc_ld_1_p5, bruncnd, brcnd);
  not not_2 (reg8_inc_ld_1_p6, reg8_inc_ld_1_p5);
  or or_4 (or_4_out, ADDRBUS[0], ADDRBUS[4]);
  ROM32x24 rom32x24_1 (
    .A4__0(reg8_inc_ld_1_p4[4:0]), .CS(1'b1),
    .DOUT({reg8_inc_ld_1_p3, rom32x24_1_dout_2, rom32x24_1_dout[11], stEXEC, stADDR, clFETCH, ldIR7__0, ldIR15__8, ldIR23__16, ldIR31__24, ldMDR, rdMEM_t, incPC, ldMAR}));
  or or_5 (or_5_out, INSTRUCBUS[16], INSTRUCBUS[17], INSTRUCBUS[18], INSTRUCBUS[22], INSTRUCBUS[19], INSTRUCBUS[21], INSTRUCBUS[20]);
  or or_6 (jmp3, INSTRUCBUS[9], INSTRUCBUS[10], INSTRUCBUS[15]);
  // DC4_16 dc4_16_1: pin names not known; wires that end beside it: rom32x24_1_dout_2, 1'b1, bruncnd, notPSWSTandFETCH, brbezadr1, brjump2, bradr2, brjump3, brnotfcmem, brgrinst, brgraddr
  and and_1 (and_1_out, ADDRBUS[0], INSTRUCBUS[21]);
  and and_2 (and_2_out, or_4_out, INSTRUCBUS[19]);
  nor nor_1 (nor_1_out, ADDRBUS[0], ADDRBUS[1], ADDRBUS[2], ADDRBUS[3], ADDRBUS[4]);
  and and_3 (and_3_out, ADDRBUS[0], INSTRUCBUS[17]);
  and and_4 (and_4_out, ADDRBUS[2], INSTRUCBUS[21]);
  and and_5 (and_5_out, or_5_out, nor_1_out);
  or or_7 (GRADDR, and_5_out, and_1_out, and_3_out, and_4_out, and_2_out);
  or or_8 (addr_t, INSTRUCBUS[16], INSTRUCBUS[17], INSTRUCBUS[18], INSTRUCBUS[22], INSTRUCBUS[19], INSTRUCBUS[21], INSTRUCBUS[20]);
  not not_3 (not_3_out, PHASEFFBUS[0]);
  not not_4 (not_4_out, PSW[0]);
  or or_9 (or_9_out, not_3_out, not_4_out);
  and and_6 (addr2, or_11_out, addr_t);
  not not_5 (not_5_out, in_3);
  and and_7 (addr4, or_10_out, addr_t);
  and and_8 (and_8_out, or_9_out, notPSWSTandFETCH);
  and and_9 (and_9_out, brjump2, jump2);
  and and_10 (and_10_out, bradr2, addr2);
  and and_11 (and_11_out, brjump3, jmp3);
  and and_12 (and_12_out, brgrinst, GRINST);
  and and_13 (and_13_out, brgraddr, GRADDR);
  and and_14 (and_14_out, brnotfcmem, not_5_out);
  or or_10 (or_10_out, ADDRBUS[0], ADDRBUS[1]);
  or or_11 (or_11_out, ADDRBUS[2], ADDRBUS[3], ADDRBUS[4]);
  and and_15 (and_15_out, brbezadr1, bezadr1);
  or or_12 (brcnd, and_8_out, and_15_out, and_9_out, and_10_out, and_11_out, and_12_out, and_13_out, and_14_out);
  or or_13 (or_13_out, INSTRUCBUS[16], INSTRUCBUS[17], INSTRUCBUS[18], INSTRUCBUS[22], INSTRUCBUS[19], INSTRUCBUS[20], INSTRUCBUS[8], INSTRUCBUS[10], INSTRUCBUS[9], INSTRUCBUS[0], INSTRUCBUS[11], INSTRUCBUS[7], INSTRUCBUS[15], INSTRUCBUS[14], INSTRUCBUS[6], INSTRUCBUS[1], INSTRUCBUS[2], INSTRUCBUS[3], INSTRUCBUS[12], INSTRUCBUS[13], INSTRUCBUS[4], INSTRUCBUS[5], INSTRUCBUS[21]);
  not not_6 (GRINST, or_13_out);
  assign CREGBUS[4] = ldIR7__0 ? 1'b1 : 1'bz;  // Controlled_Buffer controlled_buffer_1
  assign CREGBUS[5] = ldIR15__8 ? 1'b1 : 1'bz;  // Controlled_Buffer controlled_buffer_2
  assign CREGBUS[6] = ldIR23__16 ? 1'b1 : 1'bz;  // Controlled_Buffer controlled_buffer_3
  assign CREGBUS[7] = ldIR31__24 ? 1'b1 : 1'bz;  // Controlled_Buffer controlled_buffer_4
  assign CMEMBUS[0] = ldMAR ? 1'b1 : 1'bz;  // Controlled_Buffer controlled_buffer_5
  assign CMEMBUS[2] = ldMDR ? 1'b1 : 1'bz;  // Controlled_Buffer controlled_buffer_6
  assign CMEMBUS[4] = incPC ? 1'b1 : 1'bz;  // Controlled_Buffer controlled_buffer_7
  assign CFFBUS[1] = clFETCH ? 1'b1 : 1'bz;  // Controlled_Buffer controlled_buffer_8
  assign CFFBUS[2] = stADDR ? 1'b1 : 1'bz;  // Controlled_Buffer controlled_buffer_9
  assign CFFBUS[4] = stEXEC ? 1'b1 : 1'bz;  // Controlled_Buffer controlled_buffer_10
  assign rdMEM = rdMEM_t ? 1'b1 : 1'bz;  // Controlled_Buffer controlled_buffer_11

  // Other names for the same wires on the sheet: immed = ADDRBUS[0]; memdir = ADDRBUS[1]; regdir = ADDRBUS[2];
  //   regind = ADDRBUS[3]; pcrel = ADDRBUS[4]; CLK = in_2; FCBUS = in_3; HALT = INSTRUCBUS[0]; RTS = INSTRUCBUS[1];
  //   RTI = INSTRUCBUS[2]; ASL = INSTRUCBUS[3]; STIVTP = INSTRUCBUS[4]; PUSH = INSTRUCBUS[5]; POP = INSTRUCBUS[6];
  //   ABS = INSTRUCBUS[7]; BR = INSTRUCBUS[8]; JMP = INSTRUCBUS[9]; JSR = INSTRUCBUS[10]; BEQL = INSTRUCBUS[11];
  //   BNEG = INSTRUCBUS[12]; BGRT = INSTRUCBUS[13]; BGREU = INSTRUCBUS[14]; JLEQ = INSTRUCBUS[15];
  //   LD = INSTRUCBUS[16]; ST = INSTRUCBUS[17]; ADD = INSTRUCBUS[18]; SWAP = INSTRUCBUS[19]; OR = INSTRUCBUS[20];
  //   JADR = INSTRUCBUS[21]; AND = INSTRUCBUS[22]; FETCH = PHASEFFBUS[0]; ADDR = PHASEFFBUS[1]; EXEC = PHASEFFBUS[2];
  //   INTR = PHASEFFBUS[3]; PSWSTART = PSW[0]; rst = in_1

  // Notes on the sheet:
  //   Operaciona jedinica
  //   Kontrolna jedinica
  //   Formiranje GRINST i GRADDR signala
endmodule

module ADDR (
  input  in_1,
  input  in_2,
  input  in_3,
  input  [3:0] PHASEFFBUS,
  input  [24:0] INSTRUCBUS,
  input  [4:0] ADDRBUS,
  output [14:0] CMEMBUS,
  output [7:0] CFFBUS,
  output [16:0] CREGBUS,
  output rdMEM
);

  wire and_1_out, and_2_out, and_3_out, and_4_out, bradr, brcnd, brnotADDR, brnotFCBUS, brSTJADR, bruncnd,
       clADDR, incMAR, ldB, ldMAR, ldMDR, ldP, mp2_8b_1_p3, mxB0, mxB1, mxMAR0, mxMAR1, not_1_out, not_3_out,
       not_4_out, rdMEM_t, reg8_inc_ld_1_p6, reg8_inc_ld_1_p7, stEXEC;
  wire [3:0] mp2_8b_1_p4;
  wire [7:0] reg8_inc_ld_1_p4;
  wire [19:12] mp2_8b_1_p2;

  not not_1 (not_1_out, in_1);
  // MP2_8b mp2_8b_1: pin names not known; wires that end beside it: bradr, {3'b000, mp2_8b_1_p2[19:15]}, mp2_8b_1_p3, {4'b0000, mp2_8b_1_p4}
  // REG8_INC_LD reg8_inc_ld_1: pin names not known; wires that end beside it: in_2, not_1_out, mp2_8b_1_p3, reg8_inc_ld_1_p4, 1'b1, reg8_inc_ld_1_p6, reg8_inc_ld_1_p7
  KMADR kmadr_1 (
    .immed(ADDRBUS[0]), .memdir(ADDRBUS[1]), .regdir(ADDRBUS[2]), .regind(ADDRBUS[3]), .Adr3__0(mp2_8b_1_p4),
    .pcrel(ADDRBUS[4]));
  or or_1 (reg8_inc_ld_1_p6, bruncnd, brcnd, bradr);
  not not_2 (reg8_inc_ld_1_p7, reg8_inc_ld_1_p6);
  ROM32X20 rom32x20_1 (
    .A4__0(reg8_inc_ld_1_p4[4:0]), .CS(1'b1),
    .DOUT({mp2_8b_1_p2, stEXEC, clADDR, incMAR, ldP, ldMDR, rdMEM_t, mxMAR1, mxB1, mxMAR0, ldMAR, mxB0, ldB}));
  // DC3_8 dc3_8_1: pin names not known; wires that end beside it: mp2_8b_1_p2[14:12], 1'b1, bruncnd, brnotADDR, brnotFCBUS, bradr, brSTJADR
  not not_3 (not_3_out, PHASEFFBUS[1]);
  not not_4 (not_4_out, in_3);
  and and_1 (and_1_out, not_3_out, brnotADDR);
  and and_2 (and_2_out, not_4_out, brnotFCBUS);
  and and_3 (and_3_out, brSTJADR, INSTRUCBUS[17]);
  and and_4 (and_4_out, brSTJADR, INSTRUCBUS[21]);
  or or_2 (brcnd, and_1_out, and_2_out, and_3_out, and_4_out);
  assign CFFBUS[3] = clADDR ? 1'b1 : 1'bz;  // Controlled_Buffer controlled_buffer_1
  assign CREGBUS[1] = mxB0 ? 1'b1 : 1'bz;  // Controlled_Buffer controlled_buffer_2
  assign CREGBUS[2] = ldB ? 1'b1 : 1'bz;  // Controlled_Buffer controlled_buffer_3
  assign CREGBUS[3] = ldP ? 1'b1 : 1'bz;  // Controlled_Buffer controlled_buffer_4
  assign CMEMBUS[0] = ldMAR ? 1'b1 : 1'bz;  // Controlled_Buffer controlled_buffer_5
  assign CMEMBUS[1] = incMAR ? 1'b1 : 1'bz;  // Controlled_Buffer controlled_buffer_6
  assign CMEMBUS[2] = ldMDR ? 1'b1 : 1'bz;  // Controlled_Buffer controlled_buffer_7
  assign CMEMBUS[5] = mxMAR0 ? 1'b1 : 1'bz;  // Controlled_Buffer controlled_buffer_8
  assign CMEMBUS[8] = mxMAR1 ? 1'b1 : 1'bz;  // Controlled_Buffer controlled_buffer_9
  assign CFFBUS[4] = stEXEC ? 1'b1 : 1'bz;  // Controlled_Buffer controlled_buffer_10
  assign rdMEM = rdMEM_t ? 1'b1 : 1'bz;  // Controlled_Buffer controlled_buffer_11
  assign CREGBUS[0] = mxB1 ? 1'b1 : 1'bz;  // Controlled_Buffer controlled_buffer_12

  // Other names for the same wires on the sheet: immed = ADDRBUS[0]; memdir = ADDRBUS[1]; regdir = ADDRBUS[2];
  //   regind = ADDRBUS[3]; pcrel = ADDRBUS[4]; CLK = in_2; FCBUS = in_3; ST = INSTRUCBUS[17]; JADR = INSTRUCBUS[21];
  //   ADDR = PHASEFFBUS[1]; rst = in_1

  // Notes on the sheet:
  //   Upravljacka jedinica
  //   Operaciona jedinica
endmodule

module EXEC (
  input  in_1,
  input  in_2,
  input  in_3,
  input  [15:0] B,
  input  [7:0] DWH,
  input  [7:0] DWL,
  input  [3:0] PHASEFFBUS,
  input  [24:0] INSTRUCBUS,
  input  [4:0] ADDRBUS,
  input  [7:0] PSW,
  output [15:0] A,
  output [16:0] ALU,
  output [14:0] CMEMBUS,
  output [7:0] CFFBUS,
  output [7:0] CPSW,
  output rdMEM,
  output wrMEM,
  output [16:0] CREGBUS
);

  wire add_t, and_1_out, and_2_out, and_3_out, and_4_out, and_5_out, and_6_out, and_7_out, and_8_out,
       and_9_out, and_10_out, and_t, asl_t, brcnd, brnotEXEC, brnotFCBUS, brnotmemdir, brnotorjmp,
       brnotregdir, bropr, brorjmp, bruncnd, clEXEC, clPSWSTART, decSP, incMAR, incSP, ldA, ldB, ldC, ldDWH,
       ldDWL, ldI, ldIVTP, ldMAR, ldMDR, ldN, ldPC, ldSTART, ldV, ldZ, mp4_16b_1_p5, mp4_16b_1_p7, mxA0,
       mxA1, mxGPR0, mxGPR1, mxGPR2, mxMAR0, mxMAR1, mxMAR2, mxMDR0, mxMDR1, mxMDR2, mxPC0, mxPC1, not_1_out,
       not_3_out, not_4_out, not_5_out, not_6_out, not_7_out, not_8_out, not_9_out, not_10_out, or_2_out,
       or_t, rdMEM_t, \reg , reg8_inc_ld_1_p3, reg8_inc_ld_1_p5, reg8_inc_ld_1_p6, reg16_ld_1_p3, stINTR,
       wrGPR, wrMEM_t, xor_2_out;
  wire [6:0] mp2_8b_1_p2, mp2_8b_1_p4;
  wire [7:0] reg8_inc_ld_1_p4;
  wire [11:9] dc3_8_1_p1;
  wire [15:0] ADDABS15__0, xor_1_out;

  // DC3_8 dc3_8_1: pin names not known; wires that end beside it: dc3_8_1_p1, 1'b1, bruncnd, brnotEXEC, brnotregdir, bropr, brnotFCBUS, brnotorjmp, brnotmemdir
  not not_1 (not_1_out, in_1);
  // REG8_INC_LD reg8_inc_ld_1: pin names not known; wires that end beside it: in_2, not_1_out, reg8_inc_ld_1_p3, reg8_inc_ld_1_p4, reg8_inc_ld_1_p5, reg8_inc_ld_1_p6
  not not_2 (reg8_inc_ld_1_p6, reg8_inc_ld_1_p5);
  // MP4_16b mp4_16b_1: pin names not known; wires that end beside it: mxA1, mxA0, B, ALU[15:0], mp4_16b_1_p5, {DWH, DWL}, mp4_16b_1_p7, 1'b1
  not not_3 (not_3_out, in_1);
  // REG16_LD reg16_ld_1: pin names not known; wires that end beside it: in_2, not_3_out, reg16_ld_1_p3, A, ldA
  or or_1 (reg8_inc_ld_1_p5, bropr, brcnd, bruncnd);
  // MP2_16b mp2_16b_1: pin names not known; wires that end beside it: in_1, mp4_16b_1_p5, reg16_ld_1_p3, {16{1'b0}}, 1'b1
  // MP2_16b mp2_16b_2: pin names not known; wires that end beside it: PSW[1], A, mp4_16b_1_p7, ADDABS15__0, 1'b1
  // MP2_8b mp2_8b_1: pin names not known; wires that end beside it: bropr, {1'b0, mp2_8b_1_p2}, reg8_inc_ld_1_p3, {1'b0, mp2_8b_1_p4}, 1'b1
  assign xor_1_out = A ^ {16{1'b1}};  // XOR_Gate xor_1, 16 bits wide
  KMOPR1 kmopr1_1 (
    .LD(INSTRUCBUS[16]), .ST(INSTRUCBUS[17]), .ADD(INSTRUCBUS[18]), .AND(INSTRUCBUS[22]),
    .OR(INSTRUCBUS[20]), .JADR(INSTRUCBUS[21]), .JMP(INSTRUCBUS[9]), .BR(INSTRUCBUS[8]),
    .BEQL(INSTRUCBUS[11]), .BNEG(INSTRUCBUS[12]), .BGRT(INSTRUCBUS[13]), .BGREU(INSTRUCBUS[14]),
    .JLEQ(INSTRUCBUS[15]), .HALT(INSTRUCBUS[0]), .ASL(INSTRUCBUS[3]), .STIVTP(INSTRUCBUS[4]),
    .PUSH(INSTRUCBUS[5]), .POP(INSTRUCBUS[6]), .JSR(INSTRUCBUS[10]), .RTS(INSTRUCBUS[1]),
    .RTI(INSTRUCBUS[2]), .ABS(INSTRUCBUS[7]), .SWAP(INSTRUCBUS[19]), .Adr6__0(mp2_8b_1_p4));
  ROM128x51 rom128x51_1 (
    .A6__0(reg8_inc_ld_1_p4[6:0]), .CS(1'b1), .DOUT50__44(mp2_8b_1_p2),
    .DOUT43__32({dc3_8_1_p1, mxGPR2, mxGPR1, mxGPR0, \reg , clEXEC, stINTR, ldDWH, ldDWL, clPSWSTART}),
    .DOUT31__0({ldIVTP, ldB, asl_t, and_t, or_t, add_t, mxPC1, mxPC0, ldPC, decSP, incSP, ldSTART, ldI, ldV, ldZ, ldN, ldC, wrGPR, wrMEM_t, rdMEM_t, incMAR, mxMDR2, mxMDR1, mxMDR0, ldMDR, mxMAR2, mxMAR1, mxMAR0, ldMAR, mxA1, mxA0, ldA}));
  // ADD16 add16_1: pin names not known; wires that end beside it: xor_1_out, ADDABS15__0, 16'h1
  ALU_ADD_AND_OR alu_add_and_or_1 (
    .Cin(1'b0), .A(A), .B(B), .add(add_t), .\or (or_t), .\and (and_t), .asl(asl_t), .F(ALU[15:0]),
    .Cout(ALU[16]));
  xor xor_2 (xor_2_out, PSW[1], PSW[2]);
  or or_2 (or_2_out, PSW[4], xor_2_out);
  and and_1 (and_1_out, PSW[4], INSTRUCBUS[11]);
  and and_2 (and_2_out, INSTRUCBUS[12], PSW[1]);
  not not_4 (not_4_out, PSW[3]);
  and and_3 (and_3_out, INSTRUCBUS[14], not_4_out);
  not not_5 (not_5_out, PHASEFFBUS[2]);
  not not_6 (not_6_out, ADDRBUS[2]);
  not not_7 (not_7_out, ADDRBUS[1]);
  not not_8 (not_8_out, brorjmp);
  not not_9 (not_9_out, in_3);
  not not_10 (not_10_out, or_2_out);
  and and_4 (and_4_out, or_2_out, INSTRUCBUS[15]);
  and and_5 (and_5_out, not_5_out, brnotEXEC);
  and and_6 (and_6_out, not_6_out, brnotregdir);
  and and_7 (and_7_out, not_7_out, brnotmemdir);
  and and_8 (and_8_out, not_8_out, brnotorjmp);
  and and_9 (and_9_out, not_9_out, brnotFCBUS);
  and and_10 (and_10_out, not_10_out, INSTRUCBUS[13]);
  or or_3 (brorjmp, and_10_out, and_4_out, and_1_out, and_2_out, and_3_out);
  or or_4 (brcnd, and_5_out, and_6_out, and_7_out, and_8_out, and_9_out);
  assign CPSW[6] = ldSTART ? 1'b1 : 1'bz;  // Controlled_Buffer controlled_buffer_1
  assign CMEMBUS[0] = ldMAR ? 1'b1 : 1'bz;  // Controlled_Buffer controlled_buffer_2
  assign CMEMBUS[1] = incMAR ? 1'b1 : 1'bz;  // Controlled_Buffer controlled_buffer_3
  assign CMEMBUS[2] = ldMDR ? 1'b1 : 1'bz;  // Controlled_Buffer controlled_buffer_4
  assign CFFBUS[6] = stINTR ? 1'b1 : 1'bz;  // Controlled_Buffer controlled_buffer_5
  assign CPSW[0] = clPSWSTART ? 1'b1 : 1'bz;  // Controlled_Buffer controlled_buffer_6
  assign CPSW[1] = ldI ? 1'b1 : 1'bz;  // Controlled_Buffer controlled_buffer_7
  assign CPSW[2] = ldV ? 1'b1 : 1'bz;  // Controlled_Buffer controlled_buffer_8
  assign CPSW[3] = ldN ? 1'b1 : 1'bz;  // Controlled_Buffer controlled_buffer_9
  assign CPSW[4] = ldZ ? 1'b1 : 1'bz;  // Controlled_Buffer controlled_buffer_10
  assign CPSW[5] = ldC ? 1'b1 : 1'bz;  // Controlled_Buffer controlled_buffer_11
  assign CREGBUS[8] = wrGPR ? 1'b1 : 1'bz;  // Controlled_Buffer controlled_buffer_12
  assign CREGBUS[9] = ldIVTP ? 1'b1 : 1'bz;  // Controlled_Buffer controlled_buffer_13
  assign CMEMBUS[3] = ldPC ? 1'b1 : 1'bz;  // Controlled_Buffer controlled_buffer_14
  assign CMEMBUS[5] = mxMAR0 ? 1'b1 : 1'bz;  // Controlled_Buffer controlled_buffer_15
  assign CMEMBUS[6] = mxMDR0 ? 1'b1 : 1'bz;  // Controlled_Buffer controlled_buffer_16
  assign CMEMBUS[7] = mxMAR2 ? 1'b1 : 1'bz;  // Controlled_Buffer controlled_buffer_17
  assign CMEMBUS[8] = mxMAR1 ? 1'b1 : 1'bz;  // Controlled_Buffer controlled_buffer_18
  assign CMEMBUS[9] = mxMDR2 ? 1'b1 : 1'bz;  // Controlled_Buffer controlled_buffer_19
  assign CMEMBUS[10] = mxMDR1 ? 1'b1 : 1'bz;  // Controlled_Buffer controlled_buffer_20
  assign CMEMBUS[11] = mxPC1 ? 1'b1 : 1'bz;  // Controlled_Buffer controlled_buffer_21
  assign CMEMBUS[12] = mxPC0 ? 1'b1 : 1'bz;  // Controlled_Buffer controlled_buffer_22
  assign CMEMBUS[13] = incSP ? 1'b1 : 1'bz;  // Controlled_Buffer controlled_buffer_23
  assign CFFBUS[5] = clEXEC ? 1'b1 : 1'bz;  // Controlled_Buffer controlled_buffer_24
  assign CREGBUS[10] = ldDWH ? 1'b1 : 1'bz;  // Controlled_Buffer controlled_buffer_25
  assign CREGBUS[11] = ldDWL ? 1'b1 : 1'bz;  // Controlled_Buffer controlled_buffer_26
  assign CREGBUS[12] = mxGPR2 ? 1'b1 : 1'bz;  // Controlled_Buffer controlled_buffer_27
  assign CMEMBUS[14] = decSP ? 1'b1 : 1'bz;  // Controlled_Buffer controlled_buffer_28
  assign CREGBUS[13] = mxGPR1 ? 1'b1 : 1'bz;  // Controlled_Buffer controlled_buffer_29
  assign CREGBUS[14] = mxGPR0 ? 1'b1 : 1'bz;  // Controlled_Buffer controlled_buffer_30
  assign CREGBUS[16] = \reg  ? 1'b1 : 1'bz;  // Controlled_Buffer controlled_buffer_31
  assign rdMEM = rdMEM_t ? 1'b1 : 1'bz;  // Controlled_Buffer controlled_buffer_32
  assign wrMEM = wrMEM_t ? 1'b1 : 1'bz;  // Controlled_Buffer controlled_buffer_33

  // Other names for the same wires on the sheet: A15__0[15:0] = A; memdir = ADDRBUS[1]; regdir = ADDRBUS[2];
  //   ALU15__0[15:0] = ALU[15:0]; C16 = ALU[16]; B15__0[15:0] = B; CLK = in_2; FCBUS = in_3; HALT = INSTRUCBUS[0];
  //   RTS = INSTRUCBUS[1]; RTI = INSTRUCBUS[2]; ASL = INSTRUCBUS[3]; STIVTP = INSTRUCBUS[4]; PUSH = INSTRUCBUS[5];
  //   POP = INSTRUCBUS[6]; ABS = INSTRUCBUS[7]; BR = INSTRUCBUS[8]; JMP = INSTRUCBUS[9]; JSR = INSTRUCBUS[10];
  //   BEQL = INSTRUCBUS[11]; BNEG = INSTRUCBUS[12]; BGRT = INSTRUCBUS[13]; BGREU = INSTRUCBUS[14];
  //   JLEQ = INSTRUCBUS[15]; LD = INSTRUCBUS[16]; ST = INSTRUCBUS[17]; ADD = INSTRUCBUS[18]; SWAP = INSTRUCBUS[19];
  //   OR = INSTRUCBUS[20]; JADR = INSTRUCBUS[21]; AND = INSTRUCBUS[22]; EXEC = PHASEFFBUS[2]; PSWN = PSW[1];
  //   PSWV = PSW[2]; PSWC = PSW[3]; PSWZ = PSW[4]; rst = in_1

  // Notes on the sheet:
  //   Operaciona jedinica
  //   Upravljacka jedinica
  //   Sabirac za ABS
  //   Akomulator
  //   ALU
  //   Uslov za skok
endmodule

module INTR (
  input  [15:0] IVTP,
  input  in_2,
  input  in_3,
  input  in_4,
  input  [3:0] PHASEFFBUS,
  input  [24:0] INSTRUCBUS,
  input  [7:0] PSW,
  input  [3:0] intr,
  output [15:0] ADDIVTP,
  output [1:0] UEXT1__0,
  output inta,
  output [14:0] CMEMBUS,
  output [7:0] CFFBUS,
  output [16:0] CREGBUS,
  output rdMEM,
  output wrMEM
);

  wire and_2_out, and_3_out, and_4_out, brcnd, brnotFCBUS, brnotINTR, brnotprekid, bruncnd, clINTR, incMAR,
       incSP, ldDWH, ldDWL, ldMAR, ldMDR, ldPC, mxGPR, mxGPR0, mxGPR1, mxGPR2, mxMAR0, mxMAR2, mxMDR0,
       mxMDR1, mxMDR2, mxPC1, not_1_out, not_2_out, not_3_out, not_4_out, not_5_out, not_6_out, or_2_out,
       prekid, prper, rdMEM_t, stFETCH, wrMEM_t;
  wire [2:0] dc3_8_1_p1;
  wire [2:1] IVTDSP15__0;
  wire [5:0] reg6_inc_ld_1_a5__0, rom64x31_1_dout;

  and and_1 (prekid, prper, 1'b1, not_2_out);
  not not_1 (not_1_out, in_2);
  // DC3_8 dc3_8_1: pin names not known; wires that end beside it: dc3_8_1_p1, 1'b1, bruncnd, brnotINTR, brnotprekid, brnotFCBUS
  not not_2 (not_2_out, INSTRUCBUS[0]);
  REG6_INC_LD reg6_inc_ld_1 (
    .I5__0(rom64x31_1_dout), .LD(or_2_out), .INC(not_3_out), .mr(not_1_out), .CLK(in_3),
    .A5__0(reg6_inc_ld_1_a5__0));
  or or_1 (prper, intr[3], intr[2], intr[1], intr[0]);
  not not_3 (not_3_out, or_2_out);
  ROM64x31 rom64x31_1 (
    .A5__0(reg6_inc_ld_1_a5__0), .CS(1'b1),
    .DOUT({rom64x31_1_dout, dc3_8_1_p1, clINTR, stFETCH, mxPC1, ldPC, ldDWH, ldDWL, incMAR, rdMEM_t, mxGPR, inta, mxMDR2, mxMDR0, wrMEM_t, ldMDR, mxMDR1, incSP, ldMAR, mxMAR2, mxGPR2, mxGPR1, mxGPR0, mxMAR0}));
  or or_2 (or_2_out, brcnd, bruncnd);
  // CD4 cd4_1: pin names not known; wires that end beside it: intr[3], intr[2], intr[1], intr[0], 1'b1, UEXT1__0[1], UEXT1__0[0]
  // REG2_LD reg2_ld_1: pin names not known; wires that end beside it: in_3, UEXT1__0, IVTDSP15__0, inta
  not not_4 (not_4_out, PHASEFFBUS[3]);
  not not_5 (not_5_out, prekid);
  not not_6 (not_6_out, in_4);
  and and_2 (and_2_out, not_4_out, brnotINTR);
  and and_3 (and_3_out, not_5_out, brnotprekid);
  and and_4 (and_4_out, not_6_out, brnotFCBUS);
  // ADD16 add16_1: pin names not known; wires that end beside it: IVTP, ADDIVTP, {{13{1'b0}}, IVTDSP15__0, 1'b0}, 1'b0
  or or_3 (brcnd, and_2_out, and_3_out, and_4_out);
  assign CMEMBUS[0] = ldMAR ? 1'b1 : 1'bz;  // Controlled_Buffer controlled_buffer_1
  assign CMEMBUS[1] = incMAR ? 1'b1 : 1'bz;  // Controlled_Buffer controlled_buffer_2
  assign CMEMBUS[2] = ldMDR ? 1'b1 : 1'bz;  // Controlled_Buffer controlled_buffer_3
  assign CMEMBUS[3] = ldPC ? 1'b1 : 1'bz;  // Controlled_Buffer controlled_buffer_4
  assign CMEMBUS[5] = mxMAR0 ? 1'b1 : 1'bz;  // Controlled_Buffer controlled_buffer_5
  assign CMEMBUS[6] = mxMDR0 ? 1'b1 : 1'bz;  // Controlled_Buffer controlled_buffer_6
  assign CMEMBUS[7] = mxMAR2 ? 1'b1 : 1'bz;  // Controlled_Buffer controlled_buffer_7
  assign CMEMBUS[9] = mxMDR2 ? 1'b1 : 1'bz;  // Controlled_Buffer controlled_buffer_8
  assign CMEMBUS[10] = mxMDR1 ? 1'b1 : 1'bz;  // Controlled_Buffer controlled_buffer_9
  assign CMEMBUS[11] = mxPC1 ? 1'b1 : 1'bz;  // Controlled_Buffer controlled_buffer_10
  assign CFFBUS[0] = stFETCH ? 1'b1 : 1'bz;  // Controlled_Buffer controlled_buffer_11
  assign CFFBUS[7] = clINTR ? 1'b1 : 1'bz;  // Controlled_Buffer controlled_buffer_12
  assign CREGBUS[10] = ldDWH ? 1'b1 : 1'bz;  // Controlled_Buffer controlled_buffer_13
  assign CREGBUS[11] = ldDWL ? 1'b1 : 1'bz;  // Controlled_Buffer controlled_buffer_14
  assign CREGBUS[12] = mxGPR2 ? 1'b1 : 1'bz;  // Controlled_Buffer controlled_buffer_15
  assign CREGBUS[13] = mxGPR1 ? 1'b1 : 1'bz;  // Controlled_Buffer controlled_buffer_16
  assign CREGBUS[14] = mxGPR0 ? 1'b1 : 1'bz;  // Controlled_Buffer controlled_buffer_17
  assign CREGBUS[15] = mxGPR ? 1'b1 : 1'bz;  // Controlled_Buffer controlled_buffer_18
  assign rdMEM = rdMEM_t ? 1'b1 : 1'bz;  // Controlled_Buffer controlled_buffer_19
  assign wrMEM = wrMEM_t ? 1'b1 : 1'bz;  // Controlled_Buffer controlled_buffer_20
  assign CMEMBUS[13] = incSP ? 1'b1 : 1'bz;  // Controlled_Buffer controlled_buffer_21

  // Other names for the same wires on the sheet: ldBR = inta; ADDIVTP15__0[15:0] = ADDIVTP; CLK = in_3; FCBUS = in_4;
  //   HALT = INSTRUCBUS[0]; intr3__0[3:0] = intr; IVTP15__0[15:0] = IVTP; INTR_t = PHASEFFBUS[3]; PSWI = PSW[5];
  //   rst = in_2

  // Notes on the sheet:
  //   Operaciona jedinica
  //   Upravljacka jedinica
endmodule

module RAM (
  input  [15:0] in_1,
  input  in_2,
  input  [7:0] in_3,
  input  in_4,
  input  in_5,
  input  in_6,
  output [7:0] out_7,
  output out_8
);

  wire and_1_out, and_2_out, CNT0, LDCNT, not_1_out, notCNT0, or_1_out, reg4_ld_sl_sr_1_p6, rsff_2_p4,
       rsff_2_p5, rsff_3_p4, sl;
  wire [3:0] CNT, LFSR;

  // RSFF rsff_1: pin names not known; wires that end beside it: 1'b0, in_2, in_6, sl
  or or_1 (or_1_out, in_4, in_5);
  // REG4_LD_SL_SR reg4_ld_sl_sr_1: pin names not known; wires that end beside it: 1'b0, 1'b0, in_2, 4'b1111, LFSR, reg4_ld_sl_sr_1_p6, sl, in_6
  // RisingEdge risingedge_1: pin names not known; wires that end beside it: or_1_out, in_2, LDCNT
  // MEM64Kx8 mem64kx8_1: pin names not known; wires that end beside it: in_1, 1'b1, in_2, in_3, out_7, in_4
  xor xor_1 (reg4_ld_sl_sr_1_p6, LFSR[2], LFSR[3]);
  and and_1 (and_1_out, CNT0, not_1_out);
  not not_1 (not_1_out, LDCNT);
  // RSFF rsff_2: pin names not known; wires that end beside it: and_1_out, in_2, LDCNT, rsff_2_p4, rsff_2_p5
  not not_2 (rsff_2_p4, in_6);
  and and_2 (and_2_out, rsff_2_p5, CNT0);
  // REG4m_DEC_LD reg4m_dec_ld_1: pin names not known; wires that end beside it: in_2, LFSR, CNT, LDCNT, notCNT0, notCNT0
  or or_2 (notCNT0, CNT[0], CNT[1], CNT[2], CNT[3]);
  // RSFF rsff_3: pin names not known; wires that end beside it: out_8, in_2, and_2_out, rsff_3_p4, out_8
  not not_3 (rsff_3_p4, in_6);
  not not_4 (CNT0, notCNT0);

  // Other names for the same wires on the sheet: ADR[15:0] = in_1; CLK = in_2; DIN[7:0] = in_3; DOUT[7:0] = out_7;
  //   fc = out_8; RDMEM = in_5; rst = in_6; WRMEM = in_4

  // Notes on the sheet:
  //   Random broj predstavlja vreme pristupa memoriji
  //   Brojac za generisanje random broja 
  //   Jedinica za generisanje function complete (fc) signala
  //   Brojac za dekrementiranje random broja
endmodule
